# Fritzing sketch board (saved by Fritzing 0.9.1b)
breadboards: 1

parts:
  Part1 = Arduino Uno (Rev3) - ICSP  # not connected
  LED1 = smd LED [color="Red (633nm)" package="0603 [SMD]"]
  LED2 = smd LED [color="Yellow (585nm)" package="0603 [SMD]"]
  LED3 = smd LED [color="Green (560nm)" package="0603 [SMD]"]
  U1 = POT [package=trim_pot]
  S2 = Pushbutton [package="[THT]"]
  S3 = Pushbutton [package="[THT]"]
  R1 = Resistor [tolerance=±5% resistance=220 package="0603 [SMD]"]
  R2 = Resistor [tolerance=±5% resistance=220 package="0603 [SMD]"]
  R3 = Resistor [tolerance=±5% resistance=220 package="0603 [SMD]"]

nets:
  N1: LED1.cathode, R1.Pin_0
  N2: LED2.cathode, R2.Pin_0
  N3: LED3.cathode, R3.Pin_0
  N4: U1.S, U1.A
  N5: S2.Pin_1, S2.Pin_2, S2.Pin_3, S2.Pin_4
  N6: S3.Pin_1, S3.Pin_2, S3.Pin_3, S3.Pin_4
